# Fritzing sketch Esp32_rele_dht_blynk (saved by Fritzing 1.0.2b)

parts:
  MH-ET_LIVE_ESP32_DEVKIT1 = MH-ET LIVE ESP32 DEVKIT 38 pins
  5VDC_Relay_K-019 = KY-019 5V Relay Module [package="Breakout board"]
  Temperature_and_Humidity_Sensor_KY-015 = KY-015 Temperature & Humidity Sensor Module [package="Breakout board"]
  220VAC_Socket = Lilypad Battery Connect
  220V_Ac_Fan = Fan - Ventilador [package=THT]

nets:
  3V3: MH-ET_LIVE_ESP32_DEVKIT1.3V3, Temperature_and_Humidity_Sensor_KY-015.Vin
  N1: MH-ET_LIVE_ESP32_DEVKIT1.5V, 5VDC_Relay_K-019.+
  N2: MH-ET_LIVE_ESP32_DEVKIT1.GND, 5VDC_Relay_K-019.-
  N3: MH-ET_LIVE_ESP32_DEVKIT1.IO4, Temperature_and_Humidity_Sensor_KY-015.S
  N4: MH-ET_LIVE_ESP32_DEVKIT1.IO2, 5VDC_Relay_K-019.S
  N5: 5VDC_Relay_K-019.Common, 220V_Ac_Fan.5V
  N6: 5VDC_Relay_K-019.NO, 220VAC_Socket.+
  N7: 220VAC_Socket.-, 220V_Ac_Fan.GND

notes:
  5V
  GND
  4
  2
  3.3 V
  NO
  C

custom parts:
  MH-ET LIVE ESP32 DEVKIT 38 pins: http://mh.nodebb.com/topic/2/mh-et-live-esp32-devkit
  KY-019 5V Relay Module: KY-019 5V Relay module, used to control AC circuits. (Special thanks to vanepp for fixing the PCB holes and other errors)
  KY-015 Temperature & Humidity Sensor Module: KY-015 temperature and humidity sensor module, provides a low-latency serial interface to measure humidity and temperature.
  Fan - Ventilador: Ventilador de 2 pines, se encuentra comunmente en computadoras de escritorio
